# Fritzing sketch auto-pumpkin (saved by Fritzing 0.9.2b)
breadboards: 1

parts:
  Part1 = Arduino Nano (Rev3.0)
  PIR1 = PIR sensor
  Part2 = Breakout Board for Electret Microphone
  Part3 = LC Studio SD Card Module
  Q1 = TRANSISTOR_NPN [package=to-92-ammo]
  Q2 = TRANSISTOR_NPN [package=to-92-ammo]
  Q3 = TRANSISTOR_NPN [package=to-92-ammo]
  Analog_RGB_LED_Strip1 = Analog RGB LED Strip
  JACK1 = 2.1mm Barrel Jack with Terminal Block
  SP1 = SPEAKER [package=pcb_mount_speaker]
  Q4 = TRANSISTOR_NPN [package=to-92-ammo]
  R1 = Resistor [tolerance=±5% resistance=220 package="2010 [SMD]"]

nets:
  GND: Part1.GND, PIR1.GND, Part2.GND, Part3.GND, Q4.E
  N1: Part1.D3, Q1.B
  N2: Part1.D4, Part3.CS
  N3: Part1.D5, Q3.B
  N4: Part1.D6, Q2.B
  N5: Part1.D7, PIR1.SIG
  N6: Part1.D9, R1.Pin_0
  N7: Part1.D11/MOSI, Part3.MOSI
  N8: Part1.D12/MISO, Part3.MISO
  5V: Part1.5V, PIR1.VDD, Part3.5V
  N9: Part1.A2, Part2.AUD
  3V3: Part1.3V3, Part2.VCC
  N10: Part1.D13/SCK, Part3.SCK
  N11: Q1.E, Q2.E, Q3.E, JACK1.NEG
  N12: Q1.C, Analog_RGB_LED_Strip1.B
  N13: Q2.C, Analog_RGB_LED_Strip1.R
  N14: Q3.C, Analog_RGB_LED_Strip1.G
  N15: Analog_RGB_LED_Strip1.12v, JACK1.POS
  N16: SP1.+, Q4.C
  N17: Q4.B, R1.Pin_1

custom parts:
  LC Studio SD Card Module: The LC Studio SD card module serves as an interface to an SD card. The module works at 3.3 volts and 5 volts. The SPI (Serial Peripheral Interface) protocol is used for communicating with the module.
  Analog RGB LED Strip: Analog RGB LED strip
